# Fritzing sketch HC-SR04-WeMos (saved by Fritzing 0.9.9b)
breadboards: 1

parts:
  WeMos_D1_Mini1 = WeMos D1 Mini  # not connected
  U1 = HC-SR04 [chip_label=IC package="SIP (Single Inline) [THT]"]
  OLED_I2C1 = OLED 128x64 I2C Monochrome Display

nets:
  VCC: U1.Vcc, OLED_I2C1.VDD
  GND: U1.GND, OLED_I2C1.GND

custom parts:
  HC-SR04: HC-SR04 ultrasound distance sensor
